# Fritzing sketch wire diagram (saved by Fritzing 0.9.3b)

parts:
  U1 = NodeMCU V1.0
  M1 = DC Motor
  S1 = H-Bridge with L298N
  M2 = DC Motor
  BATT1 = LiPoly Battery (1300mAh)

nets:
  N1: U1.D0, S1.ENA
  N2: U1.D1, S1.IN1
  N3: U1.D2, S1.IN2
  N4: U1.D5, S1.ENB
  N5: U1.D6, S1.IN3
  N6: U1.D7, S1.IN4
  GND: U1.GND, S1.GND, BATT1.negative
  VIN: U1.Vin, S1.5V
  N7: M1.pin_1, S1.M2-02
  N8: M1.pin_2, S1.M2-01
  N9: S1.12V, BATT1.positive
  N10: S1.M1-01, M2.pin_2
  N11: S1.M1-02, M2.pin_1

custom parts:
  NodeMCU V1.0: ESP8266 based NodeMCU
  H-Bridge with L298N: h-bridge
  LiPoly Battery (1300mAh): Lithium Ion Polymer Battery (1300mAh)
